// Logisim project MINICS2.circ as structural Verilog: 6 circuits, main circuit main
// PC
module main (
  output [3:0] IMMEDIATE,
  output [3:0] RESULT,
  output [3:0] R0,
  output LI_0,
  output [3:0] R1,
  output [3:0] R2,
  output [3:0] R3,
  output [3:0] ALU_result,
  output [1:0] Rz,
  output N__last_CMP_was__0,
  output update,
  output [1:0] Ry,
  output [1:0] Rx,
  output Z__last_CMP_was__0,
  output Branch,
  output [7:0] INSTRUCTION
);

  wire and_1_out, and_2_out, and_3_out, and_4_out, clock_1_out, decoder_1_out0, decoder_1_out1,
       decoder_1_out2, decoder_1_out3, inst_decoder_1_alu_operation_select,
       inst_decoder_1_load_condition_code;
  wire [1:0] inst_decoder_1_jump_condition;
  wire [3:0] inst_decoder_1_jump_offset, multiplexer_1_out, multiplexer_2_out, multiplexer_3_out,
       pc_1_program_counter;

  Decoder #(.select(2)) decoder_1 (
    .out0(decoder_1_out0), .out1(decoder_1_out1), .out2(decoder_1_out2), .out3(decoder_1_out3), .sel(Rz),
    .en(1'b1));
  inst_decoder inst_decoder_1 (
    .immed(IMMEDIATE), .register_source_select(LI_0), .dest(Rz), .register_load_enable(update), .src2(Ry),
    .src1(Rx), .ALU_operation_select(inst_decoder_1_alu_operation_select), .in_1(INSTRUCTION),
    .load_condition_code(inst_decoder_1_load_condition_code), .jump_condition(inst_decoder_1_jump_condition),
    .jump_enable(Branch), .jump_offset(inst_decoder_1_jump_offset));
  Multiplexer #(.width(4)) multiplexer_1 (
    .in0(IMMEDIATE), .in1(ALU_result), .out(multiplexer_1_out), .sel(LI_0), .en(1'b1));
  and and_1 (and_1_out, decoder_1_out0, update);
  and and_2 (and_2_out, decoder_1_out1, update);
  and and_3 (and_3_out, decoder_1_out2, update);
  and and_4 (and_4_out, decoder_1_out3, update);
  Clock clock_1 (.out(clock_1_out));
  Register #(.width(4)) register_1 (.D(multiplexer_1_out), .en(and_1_out), .Q(R0), .clk(clock_1_out), .clr(1'b0));
  Register #(.width(4)) register_2 (.D(multiplexer_1_out), .en(and_2_out), .Q(R1), .clk(clock_1_out), .clr(1'b0));
  Register #(.width(4)) register_3 (.D(multiplexer_1_out), .en(and_3_out), .Q(R2), .clk(clock_1_out), .clr(1'b0));
  Register #(.width(4)) register_4 (.D(multiplexer_1_out), .en(and_4_out), .Q(R3), .clk(clock_1_out), .clr(1'b0));
  Multiplexer #(.select(2), .width(4)) multiplexer_2 (
    .in0(R0), .in1(R1), .in2(R2), .in3(R3), .out(multiplexer_2_out), .sel(Rx), .en(1'b1));
  Multiplexer #(.select(2), .width(4)) multiplexer_3 (
    .in0(R0), .in1(R1), .in2(R2), .in3(R3), .out(multiplexer_3_out), .sel(Ry), .en(1'b1));
  ALU alu_1 (
    .operand1(multiplexer_2_out), .operand2(multiplexer_3_out),
    .ADD__0____SUB__1(inst_decoder_1_alu_operation_select), .result(ALU_result));
  CC condition_code_register (
    .Load_CC(inst_decoder_1_load_condition_code), .data_in(ALU_result), .Z(Z__last_CMP_was__0),
    .N(N__last_CMP_was__0), .Clock(clock_1_out));
  PC pc_1 (
    .Condition(inst_decoder_1_jump_condition), .Jump(Branch), .Offset(inst_decoder_1_jump_offset),
    .Is_zero(Z__last_CMP_was__0), .Is_negative(N__last_CMP_was__0), .Clock(clock_1_out),
    .Program_Counter(pc_1_program_counter));
  ROM #(.addrWidth(4)) rom_1 (.addr(pc_1_program_counter), .data(INSTRUCTION), .sel(1'b1));

  assign RESULT = ALU_result;

  // Notes on the sheet:
  //   ADDU/SUBU=1
  //   instruction
  //   decoder
  //   REGISTERS
  //   CLOCK
  //   ALU
  //   MINICS2 processor
  //   PC
  //   INSTRUCTION MEMORY
  //   contents of rom_1 (hex, n*v repeats v):
  //   0 11 20 33 ce e3 69 42 fb ff
endmodule

module CC (
  input  [3:0] data_in,
  input  Load_CC,
  input  Clock,
  output Z,
  output N
);

  wire not_1_out;
  wire [1:0] multiplexer_1_out;
  wire [1:1] nor_1_out;

  not not_1 (not_1_out, Load_CC);
  Multiplexer #(.width(2)) multiplexer_1 (
    .in0({nor_1_out[1], data_in[3]}), .in1({Z, N}), .out(multiplexer_1_out), .sel(not_1_out), .en(1'b1));
  nor nor_1 (nor_1_out[1], data_in[3], data_in[2], data_in[1], data_in[0]);
  Register #(.width(2)) register_1 (.D(multiplexer_1_out), .en(1'b1), .Q({Z, N}), .clk(Clock), .clr(1'b0));

  // Notes on the sheet:
  //   is negative
  //   is zero
endmodule

module ALU (
  input  [3:0] operand1,
  input  [3:0] operand2,
  input  ADD__0____SUB__1,
  output [3:0] result
);

  wire [3:0] multiplexer_1_out, not_1_out;

  assign not_1_out = ~operand2;  // NOT_Gate not_1, 4 bits wide
  Multiplexer #(.width(4)) multiplexer_1 (
    .in0(operand2), .in1(not_1_out), .out(multiplexer_1_out), .sel(ADD__0____SUB__1), .en(1'b1));
  Adder #(.width(4)) adder_1 (.a(operand1), .b(multiplexer_1_out), .out(result), .cin(ADD__0____SUB__1));  // open: cout
endmodule

module PC (
  input  Is_zero,
  input  Is_negative,
  input  [1:0] Condition,
  input  Jump,
  input  [3:0] Offset,
  input  Clock,
  output [3:0] Program_Counter
);

  wire and_1_out, and_2_out, and_3_out, and_4_out, not_1_out, not_2_out, or_1_out;
  wire [3:0] adder_1_out, multiplexer_1_out;

  and and_1 (and_1_out, Condition[1], Condition[0]);
  and and_2 (and_2_out, Jump, or_1_out);
  not not_1 (not_1_out, Condition[0]);
  not not_2 (not_2_out, Condition[0]);
  and and_3 (and_3_out, not_2_out, Condition[1], Is_negative);
  and and_4 (and_4_out, Condition[1], not_1_out, Is_zero);
  or or_1 (or_1_out, and_1_out, and_4_out, and_3_out);
  Multiplexer #(.width(4)) multiplexer_1 (
    .in0(4'b0000), .in1(Offset), .out(multiplexer_1_out), .sel(and_2_out), .en(1'b1));
  Adder #(.width(4)) adder_1 (.a(multiplexer_1_out), .b(Program_Counter), .out(adder_1_out), .cin(1'b1));  // open: cout
  latched_register latched_register_1 (
    .in(adder_1_out), .load(1'b1), .clock(Clock), .reset(1'b0), .out(Program_Counter));

  // Notes on the sheet:
  //   CONDITIONS
  //   00 NEVER
  //   01 IF NEGATIVE
  //   10 IF ZERO
  //   11 ALWAYS
endmodule

module inst_decoder (
  input  [7:0] in_1,
  output [3:0] immed,
  output [1:0] dest,
  output [1:0] src2,
  output [1:0] src1,
  output register_source_select,
  output register_load_enable,
  output ALU_operation_select,
  output load_condition_code,
  output [1:0] jump_condition,
  output jump_enable,
  output [3:0] jump_offset
);

  wire not_1_out, not_2_out;

  xor xor_1 (register_source_select, in_1[7], in_1[6]);
  nand nand_1 (register_load_enable, in_1[7], in_1[6]);
  not not_1 (not_1_out, in_1[5]);
  not not_2 (not_2_out, in_1[4]);
  and and_1 (load_condition_code, in_1[7], in_1[6], not_1_out, not_2_out);
  and and_2 (jump_enable, in_1[7], in_1[6]);

  assign ALU_operation_select = in_1[7];
  assign dest = in_1[5:4];
  assign immed = in_1[3:0];
  assign jump_condition = in_1[5:4];
  assign jump_offset = in_1[3:0];
  assign src1 = in_1[3:2];
  assign src2 = in_1[1:0];
endmodule

module latched_register (
  input  [3:0] in,
  input  load,
  input  clock,
  input  reset,
  output [3:0] out
);

  wire not_1_out;
  wire [3:0] multiplexer_1_out, register_1_q;

  Multiplexer #(.width(4), .enable("false")) multiplexer_1 (.in0(out), .in1(in), .out(multiplexer_1_out), .sel(load));
  Register #(.width(4)) register_1 (.D(multiplexer_1_out), .Q(register_1_q), .clk(clock), .clr(reset));  // open: en
  Register #(.width(4)) register_2 (.D(register_1_q), .Q(out), .clk(not_1_out), .clr(reset));  // open: en
  not not_1 (not_1_out, clock);
endmodule
